// Logisim project hw4part3.circ as structural Verilog: 2 circuits, main circuit Reduced State Machine
module Tester (
  input  G
);

  wire Clock_out, reduced_state_machine_1_w, reduced_state_machine_1_x, reduced_state_machine_1_y,
       reduced_state_machine_1_z, Reset_out;

  Reduced_State_Machine reduced_state_machine_1 (
    .W(reduced_state_machine_1_w), .Clock(Clock_out), .Reset(Reset_out), .G(G),
    .X(reduced_state_machine_1_x), .Y(reduced_state_machine_1_y), .Z(reduced_state_machine_1_z));
  Clock Clock (.out(Clock_out));
  LED W (.in(reduced_state_machine_1_w));
  LED X (.in(reduced_state_machine_1_x));
  LED Y (.in(reduced_state_machine_1_y));
  LED Z (.in(reduced_state_machine_1_z));
  Button Reset (.out(Reset_out));

  // Notes on the sheet:
  //   You can use this to test your circuit.
endmodule

module Reduced_State_Machine (
  input  G,
  input  Clock,
  input  Reset,
  output W,
  output X,
  output Y,
  output Z
);

  wire and_1_out, and_2_out, and_3_out, and_4_out, and_5_out, and_6_out, and_7_out, and_8_out, and_9_out,
       and_10_out, and_11_out, and_12_out, and_13_out, and_14_out, and_15_out, and_16_out, and_17_out, D0,
       D1, D2, not_1_out, not_2_out, not_3_out, not_4_out, not_5_out, not_6_out, not_7_out, not_8_out,
       not_9_out, not_10_out, not_11_out, not_12_out, not_13_out, not_14_out, not_15_out, not_16_out, Q0, Q2;

  not not_1 (not_1_out, Q0);
  and and_1 (and_1_out, not_1_out, not_2_out, Q2);
  not not_2 (not_2_out, W);
  not not_3 (not_3_out, Q0);
  not not_4 (not_4_out, W);
  and and_2 (and_2_out, not_3_out, not_4_out, G);
  and and_3 (and_3_out, W, not_5_out);
  not not_5 (not_5_out, Q2);
  and and_4 (and_4_out, Q0, not_6_out);
  not not_6 (not_6_out, G);
  and and_5 (and_5_out, W, not_7_out, not_8_out);
  not not_7 (not_7_out, Q2);
  not not_8 (not_8_out, G);
  and and_6 (and_6_out, Q0, Q2);
  not not_9 (not_9_out, Q0);
  and and_7 (and_7_out, not_9_out, W, G);
  not not_10 (not_10_out, W);
  and and_8 (and_8_out, not_10_out, Q2);
  and and_9 (and_9_out, Q2, G);
  and and_10 (and_10_out, Q0, G);
  or or_1 (D0, and_1_out, and_2_out, and_3_out);
  or or_2 (D1, and_4_out, and_5_out, and_6_out, and_7_out);
  or or_3 (D2, and_8_out, and_9_out, and_10_out);
  Register #(.width(3)) register_1 (.D({D2, D1, D0}), .Q({Q2, W, Q0}), .clk(Clock), .clr(Reset));  // open: en
  not not_11 (not_11_out, Q0);
  not not_12 (not_12_out, W);
  not not_13 (not_13_out, Q2);
  not not_14 (not_14_out, W);
  not not_15 (not_15_out, Q0);
  not not_16 (not_16_out, Q2);
  and and_11 (and_11_out, not_11_out, not_12_out, not_13_out);
  and and_12 (and_12_out, Q0, W);
  and and_13 (and_13_out, Q0, Q2);
  and and_14 (and_14_out, Q0, W);
  and and_15 (and_15_out, W, Q2);
  and and_16 (and_16_out, not_14_out, Q2);
  and and_17 (and_17_out, not_15_out, W, not_16_out);
  or or_4 (X, and_11_out, and_12_out);
  or or_5 (Y, and_13_out, and_14_out, and_15_out);
  or or_6 (Z, and_16_out, and_17_out);

  // Other names for the same wires on the sheet: Q1 = W; CLK = Clock; RST = Reset

  // Notes on the sheet:
  //   My name is
  //   Jesse Chen
  //   and this is my pretty reduced state machine!
endmodule
