// Logisim project lab5.circ as structural Verilog: 3 circuits, main circuit Easy
module Easy (
  input  A,
  input  B,
  input  C,
  output Out
);

  wire and_1_out, and_2_out, not_1_out;

  not not_1 (not_1_out, B);
  and and_1 (and_1_out, A, not_1_out);
  and and_2 (and_2_out, B, C);
  or or_1 (Out, and_1_out, and_2_out);
endmodule

module Medium (
  input  A,
  input  B,
  input  C,
  output Out
);

  wire and_1_out, and_2_out, not_1_out, not_2_out;

  not not_1 (not_1_out, B);
  not not_2 (not_2_out, C);
  and and_1 (and_1_out, B, C);
  and and_2 (and_2_out, not_1_out, not_2_out);
  or or_1 (Out, A, and_1_out, and_2_out);
endmodule

module Hard (
  input  A,
  input  B,
  input  C,
  input  D,
  output Out
);

  wire and_1_out, and_2_out, and_3_out, and_4_out, not_1_out, not_2_out, not_3_out, not_4_out, not_5_out,
       not_6_out, not_7_out, not_8_out;

  not not_1 (not_1_out, A);
  not not_2 (not_2_out, B);
  not not_3 (not_3_out, D);
  not not_4 (not_4_out, A);
  not not_5 (not_5_out, D);
  not not_6 (not_6_out, C);
  not not_7 (not_7_out, D);
  not not_8 (not_8_out, B);
  and and_1 (and_1_out, not_1_out, not_2_out, not_3_out);
  and and_2 (and_2_out, not_4_out, C, not_5_out);
  and and_3 (and_3_out, A, not_6_out, not_7_out);
  and and_4 (and_4_out, A, not_8_out);
  or or_1 (Out, and_1_out, and_2_out, and_3_out, and_4_out);
endmodule
