// Logisim project timedlab1.circ as structural Verilog: 2 circuits, main circuit main
module main (
  input  RST,
  input  A
);

  wire CLK_out, statemachine_1_w, statemachine_1_x, statemachine_1_y, statemachine_1_z;

  Clock CLK (.out(CLK_out));
  LED W (.in(statemachine_1_w));
  LED Y (.in(statemachine_1_y));
  LED X (.in(statemachine_1_x));
  statemachine statemachine_1 (
    .CLK(CLK_out), .RST(RST), .A(A), .W(statemachine_1_w), .X(statemachine_1_x), .Y(statemachine_1_y),
    .Z(statemachine_1_z));
  LED Z (.in(statemachine_1_z));
endmodule

module statemachine (
  input  CLK,
  input  RST,
  input  A,
  output W,
  output X,
  output Y,
  output Z
);

  wire and_1_out, and_2_out, and_3_out, and_4_out, and_5_out, and_6_out, D1, D2, D3, D4, Init, nA, or_1_out,
       Q1;
  wire [0:0] or_5_out;

  not not_1 (nA, A);
  not not_2 (Init, or_1_out);
  or or_1 (or_1_out, Z, D1, D2, D3, D4);
  and and_1 (and_1_out, A, Q1);
  or or_2 (D2, and_1_out, and_2_out);
  and and_2 (and_2_out, A, X);
  and and_3 (and_3_out, nA, Q1);
  or or_3 (D3, and_3_out, and_4_out);
  and and_4 (and_4_out, nA, Y);
  and and_5 (and_5_out, nA, X);
  or or_4 (D4, and_5_out, and_6_out);
  and and_6 (and_6_out, A, Y);
  or or_5 (or_5_out[0], Init, Z);
  Register #(.width(5)) register_1 (
    .D({D4, D3, D2, D1, or_5_out[0]}), .Q({Z, Y, X, Q1, D1}), .clk(CLK), .clr(RST));  // open: en
  or or_6 (W, Q1, Z);

  // Other names for the same wires on the sheet: Q0 = D1; Q2 = X; Q3 = Y; D0 = Z; Q4 = Z

  // Notes on the sheet:
  //   Hello! My name is 
  //   Jesse Chen
  //   And this is my pretty state machine!
endmodule
